# Fritzing sketch standalone_arduino (saved by Fritzing 0.9.2b)
breadboards: 1

parts:
  U2 = atmega168 [package=dip]
  XTAL2 = Crystal [frequency="16 Mhz" package=THT]
  C5 = Ceramic Capacitor [capacitance=100nF package="100 mil [THT, multilayer]"]
  C6 = Ceramic Capacitor [capacitance=100nF package="100 mil [THT, multilayer]"]
  R1 = Resistor [tolerance=±5% resistance=220 package=THT]
  S1 = Pushbutton [package="[THT]"]

nets:
  N1: U2.RESET, R1.Pin_1
  5V: U2.VCC, U2.AVCC, U2.AREF, R1.Pin_0, S1.Pin_1, S1.Pin_2
  GND: U2.GND, C5.0, C6.0, S1.Pin_3, S1.Pin_4
  N2: U2.XLAT1, XTAL2.pin_0, C5.1
  N3: U2.XLAT2, XTAL2.pin_1, C6.1
