# Fritzing sketch double_h_bridge (saved by Fritzing 0.9.2b)
circuit board: 9.74192cm x 9.31344cm
breadboards: 1

parts:
  R1 = Resistor [tolerance=±5% resistance=1 package=THT]
  R2 = Resistor [tolerance=±5% resistance=1k package=THT]
  Q1 = NPN-Transistor [package="TO92 [THT]"]
  Q2 = NPN-Transistor [package="TO92 [THT]"]
  Q3 = pnp-Powertransistor [package="TO220 [THT]"]
  Q4 = pnp-Powertransistor [package="TO220 [THT]"]
  R3 = Resistor [tolerance=±5% resistance=1 package=THT]
  R4 = Resistor [tolerance=±5% resistance=1 package=THT]
  Q5 = npn-Powertransistor [package="TO220 [THT]"]
  J1 = female pin header, 2 pins [form="♀ (female)"]
  D1 = Rectifier Diode [part_number=1N4001 package="300 mil [THT]"]
  D2 = Rectifier Diode [part_number=1N4001 package="300 mil [THT]"]
  D3 = Rectifier Diode [part_number=1N4001 package="300 mil [THT]"]
  Q7 = NPN-Transistor [package="TO92 [THT]"]
  Q8 = NPN-Transistor [package="TO92 [THT]"]
  R5 = Resistor [tolerance=±5% resistance=1 package=THT]
  R6 = Resistor [tolerance=±5% resistance=1 package=THT]
  R7 = Resistor [tolerance=±5% resistance=1 package=THT]
  R8 = Resistor [tolerance=±5% resistance=1k package=THT]
  Q9 = pnp-Powertransistor [package="TO220 [THT]"]
  Q10 = pnp-Powertransistor [package="TO220 [THT]"]
  Q11 = npn-Powertransistor [package="TO220 [THT]"]
  J2 = female pin header, 2 pins [form="♀ (female)"]
  D5 = Rectifier Diode [part_number=1N4001 package="300 mil [THT]"]
  D6 = Rectifier Diode [part_number=1N4001 package="300 mil [THT]"]
  D7 = Rectifier Diode [part_number=1N4001 package="300 mil [THT]"]
  D8 = Rectifier Diode [part_number=1N4001 package="300 mil [THT]"]
  U1 = TLP621 [package=THT]
  VCC1 = Battery
  U2 = TLP621 [package=THT]
  U3 = TLP621 [package=THT]
  U4 = TLP621 [package=THT]
  J3 = female pin header, 5 pins [form="♀ (female)"]
  D4 = Rectifier Diode [part_number=1N4001 package="300 mil [THT]"]
  Q12 = npn-Powertransistor [package="TO220 [THT]"]
  Q13 = npn-Powertransistor [package="TO220 [THT]"]

nets:
  N1: R1.Pin_0, U1.Pin_3
  N2: R1.Pin_1, Q1.B
  N3: R2.Pin_0, Q2.B
  N4: R2.Pin_1, U2.Pin_3
  N5: Q1.E, Q13.base
  N6: Q1.C, R3.Pin_1
  N7: Q2.E, Q5.base
  N8: Q2.C, R4.Pin_1
  N9: Q3.base, R3.Pin_0
  N10: Q3.collector, Q5.collector, J1.pin2, D2.anode, D3.cathode
  N11: Q3.emitter, Q4.emitter, D1.cathode, D2.cathode, Q9.emitter, Q10.emitter, D5.cathode, D6.cathode, U1.Pin_4, VCC1.+, U2.Pin_4, U3.Pin_4, U4.Pin_4
  N12: Q4.base, R4.Pin_0
  N13: Q4.collector, J1.pin1, D1.anode, D4.cathode, Q13.collector
  N14: Q5.emitter, D3.anode, Q11.emitter, D7.anode, D8.anode, VCC1.-, D4.anode, Q12.emitter, Q13.emitter
  N15: Q7.E, Q12.base
  N16: Q7.B, R5.Pin_1
  N17: Q7.C, R6.Pin_1
  N18: Q8.E, Q11.base
  N19: Q8.B, R8.Pin_0
  N20: Q8.C, R7.Pin_1
  N21: R5.Pin_0, U3.Pin_3
  N22: R6.Pin_0, Q9.base
  N23: R7.Pin_0, Q10.base
  N24: R8.Pin_1, U4.Pin_3
  N25: Q9.collector, Q11.collector, J2.pin2, D6.anode, D7.cathode
  N26: Q10.collector, J2.pin1, D5.anode, D8.cathode, Q12.collector
  N27: U1.Pin_1, J3.pin5
  N28: U1.Pin_2, U2.Pin_2, U3.Pin_2, U4.Pin_2, J3.pin1
  N29: U2.Pin_1, J3.pin4
  N30: U3.Pin_1, J3.pin3
  N31: U4.Pin_1, J3.pin2
