# Fritzing sketch h_bridge (saved by Fritzing 0.9.2b)
circuit board: 3.68158cm x 8.40513cm
breadboards: 1

parts:
  Q7 = NPN-Transistor [package="TO92 [THT]"]
  Q8 = NPN-Transistor [package="TO92 [THT]"]
  R5 = Resistor [tolerance=±5% resistance=1 package=THT]
  R6 = Resistor [tolerance=±5% resistance=1 package=THT]
  R7 = Resistor [tolerance=±5% resistance=1 package=THT]
  R8 = Resistor [tolerance=±5% resistance=1k package=THT]
  Q9 = pnp-Powertransistor [package="TO220 [THT]"]
  Q10 = pnp-Powertransistor [package="TO220 [THT]"]
  Q11 = npn-Powertransistor [package="TO220 [THT]"]
  J2 = female pin header, 2 pins [form="♀ (female)"]
  D5 = Rectifier Diode [part_number=1N4001 package="300 mil [THT]"]
  D6 = Rectifier Diode [part_number=1N4001 package="300 mil [THT]"]
  D7 = Rectifier Diode [part_number=1N4001 package="300 mil [THT]"]
  D8 = Rectifier Diode [part_number=1N4001 package="300 mil [THT]"]
  Q12 = npn-Powertransistor [package="TO220 [THT]"]

nets:
  N1: Q7.E, Q12.base
  N2: Q7.B, R5.Pin_1
  N3: Q7.C, R6.Pin_1
  N4: Q8.E, Q11.base
  N5: Q8.B, R8.Pin_0
  N6: Q8.C, R7.Pin_1
  N7: R6.Pin_0, Q9.base
  N8: R7.Pin_0, Q10.base
  N9: Q9.collector, Q11.collector, J2.pin2, D6.anode, D7.cathode
  N10: Q9.emitter, Q10.emitter, D5.cathode, D6.cathode
  N11: Q10.collector, J2.pin1, D5.anode, D8.cathode, Q12.collector
  N12: Q11.emitter, D7.anode, D8.anode, Q12.emitter
